// Digital circuit 8bitPC.dig as structural Verilog
module _8bitPC (
);

  wire and_1_out, and_2_out, and_3_out, and_4_out, and_5_out, and_6_out, and_7_out, and_8_out, and_9_out,
       and_10_out, and_11_out, and_12_out, and_13_out, and_14_out, and_15_out, and_16_out, and_17_out,
       and_18_out, and_19_out, and_20_out, and_21_out, and_22_out, and_23_out, driver_1_out, driver_2_out,
       driver_3_out, driver_4_out, driver_5_out, driver_6_out, driver_7_out, driver_8_out, driver_9_out,
       driver_10_out, driver_11_out, driver_12_out, driver_13_out, driver_14_out, driver_15_out,
       driver_16_out, driver_17_out, driver_18_out, driver_19_out, driver_20_out, driver_21_out,
       driver_22_out, driver_23_out, driver_24_out, driver_25_out, driver_26_out, driver_27_out,
       driver_28_out, driver_29_out, driver_30_out, driver_31_out, driver_32_out, driver_33_out,
       driver_34_out, driver_35_out, driver_36_out, driver_37_out, driver_38_out, driver_39_out,
       driver_40_out, driver_41_out, driver_42_out, driver_43_out, driver_44_out, driver_45_out,
       driver_46_out, driver_47_out, driver_48_out, nand_1_out, nand_2_out, nand_3_out, nand_4_out,
       nand_5_out, nand_6_out, nand_7_out, nand_8_out, nand_9_out, nand_10_out, nand_11_out, nand_12_out,
       nand_13_out, nand_14_out, nand_15_out, nand_16_out, nand_17_out, nand_18_out, nand_19_out,
       nand_20_out, nand_21_out, nand_22_out, nand_23_out, nand_24_out, nand_25_out, nand_26_out,
       nand_27_out, nand_28_out, nand_29_out, nand_30_out, nand_31_out, nand_32_out, nand_33_out,
       nand_34_out, nand_35_out, nand_36_out, nand_37_out, nand_38_out, nand_39_out, nand_40_out,
       nand_41_out, nand_42_out, nand_43_out, nand_44_out, nand_45_out, nand_46_out, nand_47_out,
       nand_48_out, nand_49_out, nand_50_out, nand_51_out, nand_52_out, nand_53_out, nand_54_out,
       nand_55_out, nand_56_out, nand_57_out, nand_58_out, nand_59_out, nand_60_out, nand_61_out,
       nand_62_out, nand_63_out, nand_64_out, nand_65_out, nand_66_out, nand_67_out, nand_68_out,
       nand_69_out, nand_70_out, nand_71_out, nand_72_out, not_1_out, not_2_out, not_3_out, not_4_out,
       not_5_out, not_6_out, not_7_out, not_8_out, not_9_out, not_10_out, not_11_out, not_12_out, not_13_out,
       not_14_out, not_15_out, not_16_out, not_17_out, not_18_out, not_19_out, not_20_out, not_21_out,
       not_22_out, not_23_out, not_24_out, not_25_out, not_26_out, not_27_out, not_28_out, not_29_out,
       not_30_out, not_31_out, not_32_out, not_33_out, not_34_out, not_35_out, not_36_out, not_37_out,
       not_38_out, not_39_out, not_40_out, not_41_out, not_42_out, not_43_out, not_44_out, not_45_out,
       not_46_out, not_47_out, not_48_out, not_49_out, not_50_out, not_51_out, not_52_out, not_53_out,
       not_54_out, not_55_out, not_56_out, not_57_out, not_58_out, not_59_out, or_1_out, or_2_out, or_3_out,
       or_4_out, or_5_out, or_6_out, or_7_out, or_8_out, or_9_out, undriven, undriven_2, undriven_3,
       undriven_4, undriven_5, undriven_6, undriven_7, undriven_8, undriven_9, undriven_10, undriven_11,
       undriven_12, undriven_13, undriven_14, undriven_15, undriven_16, undriven_17, undriven_18,
       undriven_19, undriven_20, undriven_21, undriven_22, undriven_23, undriven_24, undriven_25,
       undriven_26, undriven_27, undriven_28, undriven_29, undriven_30, undriven_31, undriven_32,
       undriven_33, undriven_34, undriven_35, undriven_36, undriven_37, undriven_38, undriven_39,
       undriven_40, undriven_41, undriven_42, undriven_43, undriven_44, undriven_45, undriven_46,
       undriven_47, undriven_48, undriven_49, undriven_50, undriven_51, undriven_52, undriven_53,
       undriven_54, undriven_55, undriven_56, xor_1_out, xor_2_out, xor_3_out, xor_4_out, xor_5_out,
       xor_6_out, xor_7_out, xor_8_out, xor_9_out, xor_10_out, xor_11_out, xor_12_out, xor_13_out,
       xor_14_out, xor_15_out, xor_16_out, xor_17_out, xor_18_out;

  xor xor_1 (xor_1_out, undriven_56, undriven_55);
  and and_1 (and_1_out, undriven_55, undriven_56);
  xor xor_2 (xor_2_out, undriven_54, undriven_53);
  and and_2 (and_2_out, undriven_53, undriven_54);
  xor xor_3 (xor_3_out, undriven_52, undriven_51);
  and and_3 (and_3_out, undriven_51, undriven_52);
  xor xor_4 (xor_4_out, undriven_50, undriven_49);
  and and_4 (and_4_out, undriven_49, undriven_50);
  xor xor_5 (xor_5_out, undriven_48, undriven_47);
  and and_5 (and_5_out, undriven_47, undriven_48);
  xor xor_6 (xor_6_out, undriven_41, undriven_42);
  and and_6 (and_6_out, undriven_42, undriven_41);
  xor xor_7 (xor_7_out, undriven_43, undriven_44);
  and and_7 (and_7_out, undriven_44, undriven_43);
  xor xor_8 (xor_8_out, undriven_45, undriven_46);
  and and_8 (and_8_out, undriven_46, undriven_45);
  xor xor_9 (xor_9_out, xor_1_out, undriven_40);
  and and_9 (and_9_out, undriven_40, xor_1_out);
  xor xor_10 (xor_10_out, xor_2_out, or_1_out);
  and and_10 (and_10_out, or_1_out, xor_2_out);
  xor xor_11 (xor_11_out, xor_3_out, or_2_out);
  and and_11 (and_11_out, or_2_out, xor_3_out);
  xor xor_12 (xor_12_out, xor_4_out, or_3_out);
  and and_12 (and_12_out, or_3_out, xor_4_out);
  xor xor_13 (xor_13_out, xor_5_out, or_4_out);
  and and_13 (and_13_out, or_4_out, xor_5_out);
  xor xor_14 (xor_14_out, xor_6_out, or_5_out);
  and and_14 (and_14_out, or_5_out, xor_6_out);
  xor xor_15 (xor_15_out, xor_7_out, or_6_out);
  and and_15 (and_15_out, or_6_out, xor_7_out);
  xor xor_16 (xor_16_out, xor_8_out, or_7_out);
  and and_16 (and_16_out, or_7_out, xor_8_out);
  or or_1 (or_1_out, and_1_out, and_9_out);
  or or_2 (or_2_out, and_2_out, and_10_out);
  or or_3 (or_3_out, and_3_out, and_11_out);
  or or_4 (or_4_out, and_4_out, and_12_out);
  or or_5 (or_5_out, and_5_out, and_13_out);
  or or_6 (or_6_out, and_6_out, and_14_out);
  or or_7 (or_7_out, and_7_out, and_15_out);
  or or_8 (or_8_out, and_8_out, and_16_out);
  not not_1 (not_1_out, undriven_39);
  and and_17 (and_17_out, undriven_37, undriven_38);
  nand nand_1 (nand_1_out, undriven_39, undriven_36);
  nand nand_2 (nand_2_out, undriven_36, not_1_out);
  xor xor_17 (xor_17_out, undriven_38, undriven_37);
  not not_2 (not_2_out, undriven_36);
  xor xor_18 (xor_18_out, xor_17_out, undriven_35);
  and and_18 (and_18_out, undriven_35, xor_17_out);
  nand nand_3 (nand_3_out, nand_1_out, nand_4_out);
  nand nand_4 (nand_4_out, nand_3_out, nand_2_out);
  or or_9 (or_9_out, and_17_out, and_18_out);
  nand nand_5 (nand_5_out, nand_3_out, not_2_out);
  not not_3 (not_3_out, nand_3_out);
  nand nand_6 (nand_6_out, not_2_out, not_3_out);
  nand nand_7 (nand_7_out, nand_5_out, nand_8_out);
  nand nand_8 (nand_8_out, nand_7_out, nand_6_out);
  not not_4 (not_4_out, undriven_34);
  and and_19 (and_19_out, not_5_out, not_10_out, not_11_out, not_9_out, not_17_out, not_18_out, not_19_out, not_16_out);
  not not_5 (not_5_out, undriven_18);
  not not_6 (not_6_out, undriven_31);
  not not_7 (not_7_out, undriven_33);
  not not_8 (not_8_out, undriven_32);
  and and_20 (and_20_out, and_19_out, undriven_15);
  not not_9 (not_9_out, undriven_14);
  not not_10 (not_10_out, undriven_17);
  not not_11 (not_11_out, undriven_16);
  not not_12 (not_12_out, undriven_27);
  not not_13 (not_13_out, undriven_30);
  not not_14 (not_14_out, undriven_29);
  not not_15 (not_15_out, undriven_28);
  and and_21 (and_21_out, not_12_out, not_15_out, not_14_out, not_13_out, not_6_out, not_8_out, not_7_out, not_4_out);
  not not_16 (not_16_out, undriven_4);
  not not_17 (not_17_out, undriven);
  not not_18 (not_18_out, undriven_2);
  not not_19 (not_19_out, undriven_3);
  not not_20 (not_20_out, undriven_26);
  not not_21 (not_21_out, undriven_25);
  not not_22 (not_22_out, undriven_24);
  not not_23 (not_23_out, undriven_23);
  not not_24 (not_24_out, undriven_21);
  not not_25 (not_25_out, undriven_22);
  not not_26 (not_26_out, undriven_19);
  not not_27 (not_27_out, undriven_20);
  and and_22 (and_22_out, not_26_out, not_27_out, not_24_out, not_25_out, not_23_out, not_22_out, not_21_out, not_20_out);
  not not_28 (not_28_out, undriven_12);
  not not_29 (not_29_out, undriven_11);
  not not_30 (not_30_out, undriven_10);
  not not_31 (not_31_out, undriven_9);
  not not_32 (not_32_out, undriven_5);
  not not_33 (not_33_out, undriven_6);
  not not_34 (not_34_out, undriven_7);
  not not_35 (not_35_out, undriven_8);
  nand nand_9 (nand_9_out, undriven_12, and_20_out);
  nand nand_10 (nand_10_out, and_20_out, not_28_out);
  nand nand_11 (nand_11_out, undriven_11, and_20_out);
  nand nand_12 (nand_12_out, and_20_out, not_29_out);
  nand nand_13 (nand_13_out, undriven_10, and_20_out);
  nand nand_14 (nand_14_out, and_20_out, not_30_out);
  nand nand_15 (nand_15_out, undriven_9, and_20_out);
  nand nand_16 (nand_16_out, and_20_out, not_31_out);
  nand nand_17 (nand_17_out, undriven_5, and_20_out);
  nand nand_18 (nand_18_out, and_20_out, not_32_out);
  nand nand_19 (nand_19_out, undriven_6, and_20_out);
  nand nand_20 (nand_20_out, and_20_out, not_33_out);
  nand nand_21 (nand_21_out, undriven_7, and_20_out);
  nand nand_22 (nand_22_out, and_20_out, not_34_out);
  nand nand_23 (nand_23_out, undriven_8, and_20_out);
  nand nand_24 (nand_24_out, and_20_out, not_35_out);
  not not_36 (not_36_out, and_20_out);
  not not_37 (not_37_out, and_20_out);
  not not_38 (not_38_out, and_20_out);
  not not_39 (not_39_out, and_20_out);
  not not_40 (not_40_out, and_20_out);
  not not_41 (not_41_out, and_20_out);
  not not_42 (not_42_out, and_20_out);
  not not_43 (not_43_out, and_20_out);
  nand nand_25 (nand_25_out, nand_9_out, nand_26_out);
  nand nand_26 (nand_26_out, nand_25_out, nand_10_out);
  nand nand_27 (nand_27_out, nand_11_out, nand_28_out);
  nand nand_28 (nand_28_out, nand_27_out, nand_12_out);
  nand nand_29 (nand_29_out, nand_13_out, nand_30_out);
  nand nand_30 (nand_30_out, nand_29_out, nand_14_out);
  nand nand_31 (nand_31_out, nand_15_out, nand_32_out);
  nand nand_32 (nand_32_out, nand_31_out, nand_16_out);
  nand nand_33 (nand_33_out, nand_17_out, nand_34_out);
  nand nand_34 (nand_34_out, nand_33_out, nand_18_out);
  nand nand_35 (nand_35_out, nand_19_out, nand_36_out);
  nand nand_36 (nand_36_out, nand_35_out, nand_20_out);
  nand nand_37 (nand_37_out, nand_21_out, nand_38_out);
  nand nand_38 (nand_38_out, nand_37_out, nand_22_out);
  nand nand_39 (nand_39_out, nand_23_out, nand_40_out);
  nand nand_40 (nand_40_out, nand_39_out, nand_24_out);
  nand nand_41 (nand_41_out, nand_25_out, not_36_out);
  not not_44 (not_44_out, nand_25_out);
  nand nand_42 (nand_42_out, not_36_out, not_44_out);
  nand nand_43 (nand_43_out, nand_27_out, not_37_out);
  not not_45 (not_45_out, nand_27_out);
  nand nand_44 (nand_44_out, not_37_out, not_45_out);
  nand nand_45 (nand_45_out, nand_29_out, not_38_out);
  not not_46 (not_46_out, nand_29_out);
  nand nand_46 (nand_46_out, not_38_out, not_46_out);
  nand nand_47 (nand_47_out, nand_31_out, not_39_out);
  not not_47 (not_47_out, nand_31_out);
  nand nand_48 (nand_48_out, not_39_out, not_47_out);
  nand nand_49 (nand_49_out, nand_33_out, not_40_out);
  not not_48 (not_48_out, nand_33_out);
  nand nand_50 (nand_50_out, not_40_out, not_48_out);
  nand nand_51 (nand_51_out, nand_35_out, not_41_out);
  not not_49 (not_49_out, nand_35_out);
  nand nand_52 (nand_52_out, not_41_out, not_49_out);
  nand nand_53 (nand_53_out, nand_37_out, not_42_out);
  not not_50 (not_50_out, nand_37_out);
  nand nand_54 (nand_54_out, not_42_out, not_50_out);
  nand nand_55 (nand_55_out, nand_39_out, not_43_out);
  not not_51 (not_51_out, nand_39_out);
  nand nand_56 (nand_56_out, not_43_out, not_51_out);
  assign driver_1_out = and_23_out ? 1'b1 : 1'bz;  // Driver driver_1
  assign driver_2_out = and_23_out ? 1'b1 : 1'bz;  // Driver driver_2
  assign driver_3_out = and_23_out ? 1'b1 : 1'bz;  // Driver driver_3
  assign driver_4_out = and_23_out ? 1'b1 : 1'bz;  // Driver driver_4
  assign driver_5_out = and_23_out ? 1'b1 : 1'bz;  // Driver driver_5
  assign driver_6_out = and_23_out ? 1'b1 : 1'bz;  // Driver driver_6
  assign driver_7_out = and_23_out ? 1'b1 : 1'bz;  // Driver driver_7
  assign driver_8_out = and_23_out ? 1'b1 : 1'bz;  // Driver driver_8
  assign driver_9_out = and_23_out ? 1'b1 : 1'bz;  // Driver driver_9
  assign driver_10_out = and_23_out ? 1'b1 : 1'bz;  // Driver driver_10
  assign driver_11_out = and_23_out ? 1'b1 : 1'bz;  // Driver driver_11
  assign driver_12_out = and_23_out ? 1'b1 : 1'bz;  // Driver driver_12
  assign driver_13_out = and_23_out ? 1'b1 : 1'bz;  // Driver driver_13
  assign driver_14_out = and_23_out ? 1'b1 : 1'bz;  // Driver driver_14
  assign driver_15_out = and_23_out ? 1'b1 : 1'bz;  // Driver driver_15
  assign driver_16_out = and_23_out ? 1'b1 : 1'bz;  // Driver driver_16
  assign driver_17_out = and_23_out ? 1'b1 : 1'bz;  // Driver driver_17
  assign driver_18_out = and_23_out ? 1'b1 : 1'bz;  // Driver driver_18
  assign driver_19_out = and_23_out ? 1'b1 : 1'bz;  // Driver driver_19
  assign driver_20_out = and_23_out ? 1'b1 : 1'bz;  // Driver driver_20
  assign driver_21_out = and_23_out ? 1'b1 : 1'bz;  // Driver driver_21
  assign driver_22_out = and_23_out ? 1'b1 : 1'bz;  // Driver driver_22
  assign driver_23_out = and_23_out ? 1'b1 : 1'bz;  // Driver driver_23
  assign driver_24_out = and_23_out ? 1'b1 : 1'bz;  // Driver driver_24
  assign driver_25_out = and_23_out ? 1'b1 : 1'bz;  // Driver driver_25
  assign driver_26_out = and_23_out ? 1'b1 : 1'bz;  // Driver driver_26
  assign driver_27_out = and_23_out ? 1'b1 : 1'bz;  // Driver driver_27
  assign driver_28_out = and_23_out ? 1'b1 : 1'bz;  // Driver driver_28
  assign driver_29_out = and_23_out ? 1'b1 : 1'bz;  // Driver driver_29
  assign driver_30_out = and_23_out ? 1'b1 : 1'bz;  // Driver driver_30
  assign driver_31_out = and_23_out ? 1'b1 : 1'bz;  // Driver driver_31
  assign driver_32_out = and_23_out ? 1'b1 : 1'bz;  // Driver driver_32
  nand nand_57 (nand_57_out, nand_41_out, nand_58_out);
  nand nand_58 (nand_58_out, nand_57_out, nand_42_out);
  nand nand_59 (nand_59_out, nand_43_out, nand_60_out);
  nand nand_60 (nand_60_out, nand_59_out, nand_44_out);
  nand nand_61 (nand_61_out, nand_45_out, nand_62_out);
  nand nand_62 (nand_62_out, nand_61_out, nand_46_out);
  nand nand_63 (nand_63_out, nand_47_out, nand_64_out);
  nand nand_64 (nand_64_out, nand_63_out, nand_48_out);
  nand nand_65 (nand_65_out, nand_49_out, nand_66_out);
  nand nand_66 (nand_66_out, nand_65_out, nand_50_out);
  nand nand_67 (nand_67_out, nand_51_out, nand_68_out);
  nand nand_68 (nand_68_out, nand_67_out, nand_52_out);
  nand nand_69 (nand_69_out, nand_53_out, nand_70_out);
  nand nand_70 (nand_70_out, nand_69_out, nand_54_out);
  nand nand_71 (nand_71_out, nand_55_out, nand_72_out);
  nand nand_72 (nand_72_out, nand_71_out, nand_56_out);
  and and_23 (and_23_out, not_52_out, not_53_out, not_54_out, not_55_out, not_56_out, not_57_out, not_59_out, not_58_out);
  not not_52 (not_52_out, undriven_13);
  not not_53 (not_53_out, undriven_13);
  not not_54 (not_54_out, undriven_13);
  not not_55 (not_55_out, undriven_13);
  not not_56 (not_56_out, undriven_13);
  not not_57 (not_57_out, undriven_13);
  assign driver_33_out = and_22_out ? nand_57_out : 1'bz;  // Driver driver_33
  assign driver_34_out = and_21_out ? nand_57_out : 1'bz;  // Driver driver_34
  assign driver_35_out = and_22_out ? nand_59_out : 1'bz;  // Driver driver_35
  assign driver_36_out = and_21_out ? nand_59_out : 1'bz;  // Driver driver_36
  assign driver_37_out = and_22_out ? nand_61_out : 1'bz;  // Driver driver_37
  assign driver_38_out = and_21_out ? nand_61_out : 1'bz;  // Driver driver_38
  assign driver_39_out = and_22_out ? nand_63_out : 1'bz;  // Driver driver_39
  assign driver_40_out = and_21_out ? nand_63_out : 1'bz;  // Driver driver_40
  assign driver_41_out = and_22_out ? nand_65_out : 1'bz;  // Driver driver_41
  assign driver_42_out = and_21_out ? nand_65_out : 1'bz;  // Driver driver_42
  assign driver_43_out = and_22_out ? nand_67_out : 1'bz;  // Driver driver_43
  assign driver_44_out = and_21_out ? nand_67_out : 1'bz;  // Driver driver_44
  assign driver_45_out = and_22_out ? nand_69_out : 1'bz;  // Driver driver_45
  assign driver_46_out = and_21_out ? nand_69_out : 1'bz;  // Driver driver_46
  assign driver_47_out = and_22_out ? nand_71_out : 1'bz;  // Driver driver_47
  assign driver_48_out = and_21_out ? nand_71_out : 1'bz;  // Driver driver_48
  not not_58 (not_58_out, undriven_13);
  not not_59 (not_59_out, undriven_13);

  // Notes on the sheet:
  //   8bitAdder
  //   FlipFlop
  //   FullAdder
endmodule
